# Fritzing sketch schematics (saved by Fritzing 0.9.3b)
circuit board: 8.46667cm x 5.64444cm

parts:
  Motor_Driver = Dual VNH2SP30 Motor Driver [part_number=MD03A]
  M1 = DC Motor [part_number="775 pro"]
  M2 = DC Motor [part_number="775 pro"]
  Processor = Arduino Nano (Rev3.0)
  Switch = SPST Switch [package=switch-spdt_lock.007s]
  Battery_12V_5Ah = Battery Holders [package=lipo-1100mAh]
  Comms = NRF24L01+ Breakout Board
  Indictor_LED = LED - 5mm [color="Red (633nm)" package="5 mm [THT]"]
  5v = Voltage Regulator [package=to-92]

nets:
  N1: Motor_Driver.1INa, Processor.D2
  N2: Motor_Driver.1INb, Processor.D4
  N3: Motor_Driver.PWM, Processor.D9
  N4: Motor_Driver.1CS, Processor.A1
  N5: Motor_Driver.+5V_(IN), Processor.5V
  N6: Motor_Driver.2CS, Processor.A0
  N7: Motor_Driver.2PWM, Processor.D10
  N8: Motor_Driver.2INb#142, Processor.D3
  N9: Motor_Driver.2INb#143, Processor.D5
  N10: Motor_Driver.2DIAG/EN, Processor.D6
  N11: Motor_Driver.OUT_1A, M1.pin_1
  N12: Motor_Driver.OUT_1B, M1.pin_2
  N13: Motor_Driver.OUT_2A, M2.pin_1
  N14: Motor_Driver.OUT_2B, M2.pin_2
  N15: Motor_Driver.VIN, Switch.P, 5v.IN
  GND: Motor_Driver.GND, Processor.GND, Switch.S, Battery_12V_5Ah.-, Comms.GND, Indictor_LED.cathode, 5v.GND
  N16: Processor.D7, Comms.CE
  N17: Processor.D8, Comms.CS
  N18: Processor.D11/MOSI, Comms.MOSI
  N19: Processor.D12/MISO, Comms.MISO
  N20: Processor.VIN, 5v.OUT
  N21: Processor.A7, Indictor_LED.anode
  3V3: Processor.3V3, Comms.VCC
  N22: Processor.D13/SCK, Comms.SCK
  N23: Switch.O, Battery_12V_5Ah.+

// code stored in the sketch: pod.ino
#include <SPI.h>
#include <DualVNH5019MotorShield.h>
#include <nRF24L01.h>
#include <RF24.h>


/*
 * Mini Pod Code
 * V 0.2
 * 
 * Carter Watts
 * 
 * Notes:
 *  Added breaking TEST
 *  Tune comfortable hand gestures
 *  
 */
 
  int led = 19;
  
//Comm
  RF24 radio (7, 8); // CE, CSN
  const byte addresses[][6] = {"AAAAA", "AAAAA"};
  char dataIn[28] = "";
  boolean dataOutB = false;
  int startInd, ind1, ind2, ind3, ind4, ind5, endInd;
  int runningB = 0;
  int x, y, z, f1, f2;
  String runningS, xS ,yS, zS, f1S, f2S;

//Motor
  unsigned char INA1 = 2;
  unsigned char INB1 = 4;
  unsigned char PWM1 = 9;
  unsigned char EN1DIAG1 = 6;
  unsigned char CS1 = A0;
  unsigned char INA2 = 3;
  unsigned char INB2 = 5;
  unsigned char PWM2 = 10;
  unsigned char EN2DIAG2 = 6;
  unsigned char CS2 = A1;
  DualVNH5019MotorShield md (INA1,
                           INB1,
                           PWM1,
                           EN1DIAG1,
                           CS1,
                           INA2,
                           INB2,
                           PWM2,
                           EN2DIAG2,
                           CS2);
                          
  //Which side of the robot the pod is - needed for arcade control
  const String LEFT = "left";
  const String RIGHT = "right";

//SET SIDE HERE FOR EVERY POD MADE-\-\-\-\-\-\-\-\-\-\-\-\-\-\-\-\-\-\-\-\-\-\-\-\-\-\-\-\-\-\-\-\-\-\-\-\-\-NOTICE-\-\-\-\-\-\-\-\-\-|
  String side = LEFT;
  //String side = RIGHT;
  
void setup() {
  
  Serial.begin(115200);
  
  pinMode(led, OUTPUT);
  
  //Radio
    radio.begin();
    radio.openWritingPipe(addresses[0]);
    radio.openReadingPipe(1, addresses[1]);
    radio.setPALevel(RF24_PA_MAX);
    
    delay(1000);
    
  //Motor Driver  
    md.init();
    Serial.println("Motor Driver Starting");

  //Startup display
    Serial.print(F("Started "));
    Serial.print(side);
    Serial.println(F(" pod"));
  
    delay(300);
    digitalWrite(led, HIGH);
    delay(300);
    digitalWrite(led, LOW);
    delay(300);
    digitalWrite(led, HIGH);
    delay(300);  
    digitalWrite(led, LOW);
    delay(300);
    
}

void loop(){

  md.init();
  digitalWrite(led, LOW);
  
  radio.startListening();
    //Reading
    if(radio.available()){
      while(radio.available())
        radio.read(&dataIn, sizeof(dataIn));

      
      //Testing
      Serial.print("Recieved: ");
      Serial.println(dataIn);
      digitalWrite(led, HIGH);

      String data = String(dataIn);
  
      //Indexing
        ind1 = data.indexOf('/');
        ind2 = data.indexOf('/',ind1+1);
        ind3 = data.indexOf('/',ind2+1);
        ind4 = data.indexOf('/',ind3+1);
        ind5 = data.indexOf('/',ind4+1);
        endInd = data.indexOf('>');
  
      //String Data
        runningS = data.substring(startInd+1,ind1);
        xS = data.substring(ind1+1,ind2);
        yS = data.substring(ind2+1,ind3);
        zS = data.substring(ind3+1,ind4);
        f1S = data.substring(ind4+1,endInd);
        f2S = data.substring(ind5+1,endInd);
      
      //Int data
        runningB = runningS.toInt();
        x = xS.toInt();
        y = yS.toInt();
        z = zS.toInt();
        f1 = f1S.toInt();
        f2 = f2S.toInt();

      if(runningB){        
        //Control motors
          if(x < 40 && x > -40)
            x = 0;
          if(y < 40 && y > -40)
            y = 0; 
                                 
          //For left
          if(side == LEFT){
            int funct = -y+x;
            //brakes
            if (funct < 30 && funct > -30){
              md.setBrakes(0,0);
            //Drive
            }else{
              int motorSpeed = map(funct, -370, 370, -400, 400);
              md.setSpeeds(motorSpeed, motorSpeed);
              //stopIfFault();
              Serial.print(F("Speed set to: "));
              Serial.println(motorSpeed);
              Serial.print(F("Funct = "));
              Serial.println(funct);
            }
          }        
        
        //For right
        if(side == RIGHT){
          int funct = y+x;
          //Brakes
          if (funct < 30 && funct > -30){
            md.setBrakes(0,0);
            //Drive
          }else{
            int motorSpeed = map(funct, -370, 370, -400, 400);
            md.setSpeeds(motorSpeed, motorSpeed);
            //stopIfFault();
            Serial.print(F("Speed set to: "));
            Serial.println(motorSpeed);
            Serial.print(F("Funct = "));
            Serial.println(funct);
          }          
        }
      }
    } 
}

void respond(String response){
  dataOutB = true;
  //Send response;

}

void stopIfFault(){
  
  if (md.getM1Fault()){
    Serial.println("M1 fault");
    delay(10);
  }
  if (md.getM2Fault()){
    Serial.println("M2 fault");
    delay(10);
  }
  
}
